// Logisim project Logisim_Simulation.circ as structural Verilog: 3 circuits, main circuit main
module main (
);

  wire and_1_out, Bit_0, Bit_1, CLK, d_ff_3_q, n7474_1_pin1, n7474_1_pin2, n7474_1_pin4, n7474_1_pin10,
       n7474_2_pin4, n7474_2_pin7, n7474_2_pin14, not_1_out, not_2_out, not_3_out, not_4_out, or_1_out,
       SN7474_Bit_0, SN7474_Bit_1, xor_1_out, xor_2_out;

  Clock clock_1 (.out(CLK));
  D_Flip_Flop d_ff_1 (.D(1'b1), .clk(CLK), .Q(Bit_0), .reset(d_ff_3_q));  // open: Qn, preset
  // Probe on Bit_0
  // Probe on Bit_1
  not not_1 (not_1_out, Bit_0);
  not not_2 (not_2_out, Bit_1);
  xor xor_1 (xor_1_out, Bit_0, Bit_1);
  D_Flip_Flop d_ff_2 (.D(Bit_0), .clk(CLK), .Q(Bit_1), .reset(d_ff_3_q));  // open: Qn, preset
  and and_1 (and_1_out, not_1_out, not_2_out);
  not not_3 (not_3_out, xor_1_out);
  // Probe on Bit_0
  // Probe on or_1_out
  or or_1 (or_1_out, and_1_out, Bit_1);
  // Probe on Bit_0
  // Probe on not_3_out
  D_Flip_Flop d_ff_3 (.D(Bit_1), .clk(CLK), .Q(d_ff_3_q), .reset(d_ff_3_q));  // open: Qn, preset
  _7474 #(.ShowInternalStructure("true")) u_7474_1 (
    .pin1(n7474_1_pin1), .pin2(n7474_1_pin2), .pin3(CLK), .pin4(n7474_1_pin4), .pin5(SN7474_Bit_0),
    .pin13(n7474_1_pin1), .pin12(SN7474_Bit_0), .pin11(CLK), .pin10(n7474_1_pin10), .pin9(SN7474_Bit_1));  // open: pin6, pin8
  _7474 #(.ShowInternalStructure("true"), .VccGndPorts("true")) u_7474_2 (
    .pin1(n7474_1_pin1), .pin2(SN7474_Bit_1), .pin3(CLK), .pin4(n7474_2_pin4), .pin6(n7474_1_pin1),
    .pin7(n7474_2_pin7), .pin14(n7474_2_pin14));  // open: pin5, pin13, pin12, pin11, pin10, pin9, pin8
  xor xor_2 (xor_2_out, SN7474_Bit_0, SN7474_Bit_1);
  not not_4 (not_4_out, xor_2_out);
  LED led_1 (.in(SN7474_Bit_0));
  LED led_2 (.in(not_4_out));
  // also tied to GND on the sheet: n7474_2_pin7
  // also tied to VCC on the sheet: {n7474_2_pin14, n7474_1_pin2, n7474_1_pin4, n7474_2_pin4, n7474_1_pin10}

  // Notes on the sheet:
  //   XOR-based solution needs more transistors than the other solution.
endmodule

module Led_Control (
  input  SN7474_Bit_0,
  input  SN7474_Bit_1
);

  wire pull_resistor_1_node, pull_resistor_2_node, pull_resistor_3_node, pull_resistor_4_node,
       pull_resistor_5_node, pull_resistor_6_node, transistor_5_out;

  Pull_Resistor #(.pull(1)) pull_resistor_1 (.node(pull_resistor_1_node));
  Transistor #(.\type ("n")) transistor_1 (.in(1'b0), .out(pull_resistor_1_node), .gate(SN7474_Bit_0));
  Pull_Resistor #(.pull(1)) pull_resistor_2 (.node(pull_resistor_2_node));
  Transistor #(.\type ("n")) transistor_2 (.in(1'b0), .out(pull_resistor_2_node), .gate(SN7474_Bit_1));
  Pull_Resistor #(.pull(1)) pull_resistor_3 (.node(pull_resistor_3_node));
  Pull_Resistor #(.pull(1)) pull_resistor_4 (.node(pull_resistor_4_node));
  Transistor #(.\type ("n")) transistor_3 (.in(1'b0), .out(pull_resistor_3_node), .gate(pull_resistor_4_node));
  Transistor #(.\type ("n")) transistor_4 (
    .in(transistor_5_out), .out(pull_resistor_4_node), .gate(pull_resistor_1_node));
  Transistor #(.\type ("n")) transistor_5 (.in(1'b0), .out(transistor_5_out), .gate(pull_resistor_2_node));
  Pull_Resistor #(.pull(1)) pull_resistor_5 (.node(pull_resistor_5_node));
  Transistor #(.\type ("n")) transistor_6 (.in(1'b0), .out(pull_resistor_5_node), .gate(pull_resistor_3_node));
  Pull_Resistor #(.pull(1)) pull_resistor_6 (.node(pull_resistor_6_node));
  Transistor #(.\type ("n")) transistor_7 (.in(1'b0), .out(pull_resistor_6_node), .gate(pull_resistor_5_node));
  Transistor #(.\type ("n")) transistor_8 (.in(1'b0), .out(pull_resistor_5_node), .gate(SN7474_Bit_1));

  // Notes on the sheet:
  //   Use 2 diodes to make the OR gate.
endmodule

module Ring_Counter (
);

  wire and_1_out, and_2_out, and_3_out, and_4_out, and_5_out, CLK_out, not_1_out, not_2_out, not_3_out,
       not_4_out, Ring_Bit_0, Ring_Bit_1, s_r_ff_1_q, s_r_ff_3_q, s_r_ff_5_q, s_r_ff_6_q, xor_1_out;

  Clock CLK (.out(CLK_out));
  S_R_Flip_Flop s_r_ff_1 (.Q(s_r_ff_1_q), .reset(s_r_ff_6_q), .preset(CLK_out));  // open: S, R, clk, Qn
  not not_1 (not_1_out, CLK_out);
  and and_1 (and_1_out, not_1_out, s_r_ff_1_q);
  S_R_Flip_Flop s_r_ff_2 (.Q(Ring_Bit_0), .reset(s_r_ff_6_q), .preset(and_1_out));  // open: S, R, clk, Qn
  xor xor_1 (xor_1_out, Ring_Bit_0, Ring_Bit_1);
  and and_2 (and_2_out, CLK_out, Ring_Bit_0);
  not not_2 (not_2_out, xor_1_out);
  S_R_Flip_Flop s_r_ff_3 (.Q(s_r_ff_3_q), .reset(s_r_ff_6_q), .preset(and_2_out));  // open: S, R, clk, Qn
  LED led_1 (.in(Ring_Bit_0));
  LED led_2 (.in(not_2_out));
  not not_3 (not_3_out, and_2_out);
  and and_3 (and_3_out, not_3_out, s_r_ff_3_q);
  S_R_Flip_Flop s_r_ff_4 (.Q(Ring_Bit_1), .reset(s_r_ff_6_q), .preset(and_3_out));  // open: S, R, clk, Qn
  and and_4 (and_4_out, CLK_out, Ring_Bit_1);
  S_R_Flip_Flop s_r_ff_5 (.Q(s_r_ff_5_q), .reset(s_r_ff_6_q), .preset(and_4_out));  // open: S, R, clk, Qn
  not not_4 (not_4_out, and_4_out);
  and and_5 (and_5_out, not_4_out, s_r_ff_5_q);
  S_R_Flip_Flop s_r_ff_6 (.Q(s_r_ff_6_q), .reset(s_r_ff_6_q), .preset(and_5_out));  // open: S, R, clk, Qn
endmodule
